# Fritzing sketch Schematic (saved by Fritzing 0.9.4)

parts:
  Компонент1 = Arduino Nano (Rev3.0)
  IR1 = TSOP312.., 314.. [package=THT]
  Q1 = NPN-Transistor [package="SOT-23 [SMD]"]
  S1 = Pushbutton [package="[THT]"]
  S2 = Pushbutton [package="[THT]"]
  S3 = Pushbutton [package="[THT]"]
  R1 = Resistor [tolerance=±5% resistance=220 package="1206 [SMD]"]  # not connected
  C1 = Capacitor [package=cap-pth-small2]
  LED2 = smd LED [color="Red (633nm)" package="1206 [SMD]"]
  C2 = Capacitor Polarized [package=cpol-radial-10uf-25v]
  Squix1 = OLED 0.96" 128x64 I2C SSD1306
  LED3 = Infrared LED - 5mm [package="5 mm [THT]"]

nets:
  GND: Компонент1.GND, Компонент1.D6, IR1.GND, S1.Pin_1, S1.Pin_2, S2.Pin_1, S2.Pin_2, S3.Pin_1, S3.Pin_2, S3.Pin_3, S3.Pin_4, C1.1, LED2.cathode, C2.-, Squix1.GND
  N1: Компонент1.D2, IR1.Data
  N2: Компонент1.D3, Q1.0
  N3: Компонент1.D5, S1.Pin_3, S1.Pin_4
  N4: Компонент1.D7, S2.Pin_3, S2.Pin_4
  N5: Компонент1.D8, IR1.Vs
  5V: Компонент1.5V, Q1.1, C1.2, C2.+, Squix1.VCC
  N6: Компонент1.A5, Squix1.SCL
  N7: Компонент1.A4, Squix1.SCA
  N8: Q1.2, LED3.anode

notes:
  220 Ohm
  10 nF
  100 uF
  NPN (2N2222)
  940 nm Infrared-Diode
  38 kHz Infrared-Receiver
  3 mm led

custom parts:
  Infrared LED - 5mm: A generic infrared LED (~1.2V)
