# Fritzing sketch Schematic (saved by Fritzing 0.9.4)

parts:
  U1 = atmega328 [package=dip]
  XTAL1 = Crystal [frequency="16 Mhz" package=THT]
  C1 = Capacitor [package=cap-pth-small2]  # not connected
  C2 = Capacitor [package=cap-pth-small2]
  C3 = Capacitor Polarized [package=cpol-radial-10uf-25v]
  C4 = Capacitor [package=cap-pth-small2]
  LED2 = smd LED [color="Red (633nm)" package="0805 [SMD]"]
  R1 = Resistor [tolerance=±5% resistance=220 package="0402 [SMD]"]
  Q1 = NPN-Transistor [package="SOT-23 [SMD]"]
  S1 = Pushbutton [package="[SMD]"]
  S2 = Pushbutton [package="[SMD]"]
  S3 = Pushbutton [package="[SMD]"]
  S4 = Pushbutton [package="[SMD]"]
  R2 = Resistor [tolerance=±5% resistance=220 package="0402 [SMD]"]
  LED3 = Infrared LED - 5mm [package="5 mm [THT]"]
  Squix1 = OLED 0.96" 128x64 I2C SSD1306
  IR1 = TSOP312.., 314.. [package=THT]

nets:
  N1: U1.RESET, S4.Pin_1, S4.Pin_2, R2.Pin_0
  N2: U1.D2, IR1.Data
  N3: U1.D3_(PWM), Q1.0
  N4: U1.D4, R1.Pin_0
  VCC: U1.VCC, U1.AVCC, C3.+, C4.2, Q1.1, R2.Pin_1, Squix1.VCC
  N5: U1.GND#7, C2.1, C3.-, S1.Pin_1, S1.Pin_2, S2.Pin_1, S2.Pin_2, S3.Pin_1, S3.Pin_2
  N6: U1.XLAT1, XTAL1.pin_1, C2.2
  N7: U1.XLAT2, XTAL1.pin_0
  N8: U1.D5_(PWM), S1.Pin_3, S1.Pin_4
  N9: U1.D6_(PWM), S2.Pin_3, S2.Pin_4
  N10: U1.D7, S3.Pin_3, S3.Pin_4
  N11: U1.D8, IR1.Vs
  GND: U1.GND#21, C4.1, LED2.cathode, S4.Pin_3, S4.Pin_4, LED3.cathode, Squix1.GND, IR1.GND
  N12: U1.A4, Squix1.SCA
  N13: U1.A5, Squix1.SCL
  N14: Q1.2, LED3.anode

notes:
  100 uF
  IR LED
  NPN 2N2222
  10 nF
  IRM3638T
  10 kOhm
  220 Ohm
  22 pF
  16 Mhz

custom parts:
  Infrared LED - 5mm: A generic infrared LED (~1.2V)
